// Logisim project computer.circ as structural Verilog: 4 circuits, main circuit datapath
module datapath (
  input  [7:0] EXTERNAL_MEMORY_DATA_BUS,
  input  RESET,
  input  CLK,
  input  [7:0] EXTERNAL_INPUT_BUS,
  input  [1:0] MUX_OPERAND2,
  input  WE_A,
  input  WE_B,
  input  WE_MBR,
  input  WE_PC,
  input  [2:0] OPCODE_ALU,
  input  WE_OUT,
  output CMP,
  output [7:0] RAM_DATA,
  output [7:0] OUTPUT_BUS,
  output [5:0] INSTRUCTION_CODE,
  output [7:0] RAM_ADDRESS
);

  wire comparator_1_eq;
  wire [7:0] alu_1_c, B_q, MBR_q, multiplexer_1_out;

  Register A (.D(alu_1_c), .en(WE_A), .clk(CLK), .Q(RAM_DATA), .clr(RESET));
  Register B (.D(alu_1_c), .en(WE_B), .clk(CLK), .Q(B_q), .clr(RESET));
  Register MBR (.D(EXTERNAL_MEMORY_DATA_BUS), .en(WE_MBR), .clk(CLK), .Q(MBR_q), .clr(RESET));
  Register PC (.D(alu_1_c), .en(WE_PC), .clk(CLK), .Q(RAM_ADDRESS), .clr(RESET));
  alu alu_1 (.A(RAM_DATA), .B(multiplexer_1_out), .OpCode(OPCODE_ALU), .C(alu_1_c));
  Multiplexer #(.select(2), .width(8)) multiplexer_1 (
    .in0(B_q), .in1(MBR_q), .in2(RAM_ADDRESS), .in3(EXTERNAL_INPUT_BUS), .out(multiplexer_1_out),
    .sel(MUX_OPERAND2));
  Comparator comparator_1 (.a({8{1'b0}}), .b(alu_1_c), .eq(comparator_1_eq));  // open: gt, lt
  Register QUT (.D(alu_1_c), .en(WE_OUT), .clk(CLK), .Q(OUTPUT_BUS), .clr(RESET));
  BitSelector #(.group(6)) bitselector_1 (.in(MBR_q), .out(INSTRUCTION_CODE), .sel(1'b0));
  D_Flip_Flop d_ff_1 (.D(comparator_1_eq), .clk(CLK), .Q(CMP), .reset(RESET));  // open: Qn, preset

  // Other names for the same wires on the sheet: R = RESET

  // Notes on the sheet:
  //   LOWEST_6_BIT_OF_MBR
  //   Compare (CMP), 1 if last ALU result was 0
endmodule

module alu (
  input  [7:0] A,
  input  [7:0] B,
  input  [2:0] OpCode,
  output [7:0] C
);

  wire [7:0] adder_1_out, adder_2_out, adder_3_out, and_1_out, or_1_out, pull_resistor_1_node,
       subtractor_1_out;

  Pull_Resistor #(.pull(1)) pull_resistor_1 (.node(pull_resistor_1_node[0]));
  Pull_Resistor pull_resistor_2 (.node(pull_resistor_1_node[7]));
  Adder adder_1 (
    .a(A), .b({{7{pull_resistor_1_node[7]}}, pull_resistor_1_node[0]}), .out(adder_1_out));  // open: cin, cout
  Adder adder_2 (
    .a(B), .b({{7{pull_resistor_1_node[7]}}, pull_resistor_1_node[0]}), .out(adder_2_out));  // open: cin, cout
  Adder adder_3 (.a(A), .b(B), .out(adder_3_out));  // open: cin, cout
  Subtractor subtractor_1 (.a(A), .b(B), .out(subtractor_1_out));  // open: bin, bout
  assign and_1_out = A & B;  // AND_Gate and_1, 8 bits wide
  assign or_1_out = A | B;  // OR_Gate or_1, 8 bits wide
  Multiplexer #(.select(3), .width(8)) multiplexer_1 (
    .in0(A), .in1(B), .in2(adder_1_out), .in3(adder_2_out), .in4(adder_3_out), .in5(subtractor_1_out),
    .in6(and_1_out), .in7(or_1_out), .out(C), .sel(OpCode));
endmodule

module controlunit (
  input  [5:0] INSTRUCTION_CODE,
  input  RESET,
  input  CMP,
  input  CLK,
  output WE_RAM,
  output [2:0] OPCODE_ALU,
  output WE_A,
  output WE_B,
  output WE_OUT,
  output WE_MBR,
  output WE_PC,
  output [1:0] MUX_OPERAND2
);

  wire [1:1] comparator_1_eq;
  wire [5:0] MPC_q, multiplexer_1_out, multiplexer_2_out;
  wire [6:0] MIR_q;
  wire [16:0] rom_1_data;

  Multiplexer #(.width(6)) multiplexer_1 (
    .in0(MIR_q[5:0]), .in1(INSTRUCTION_CODE), .out(multiplexer_1_out), .sel(MIR_q[6]));
  Register #(.width(6)) MPC (.D(multiplexer_1_out), .en(1'b1), .clk(CLK), .Q(MPC_q), .clr(RESET));
  Comparator #(.width(6)) comparator_1 (.a(MPC_q), .b(6'b010011), .eq(comparator_1_eq[1]));  // open: gt, lt
  Multiplexer #(.select(2), .width(6)) multiplexer_2 (
    .in0(MPC_q), .in1(MPC_q), .in2(6'b010100), .in3(6'b001111), .out(multiplexer_2_out),
    .sel({comparator_1_eq[1], CMP}));
  ROM #(.addrWidth(6), .dataWidth(17)) rom_1 (.addr(multiplexer_2_out), .data(rom_1_data));
  Comparator #(.width(6)) comparator_2 (.a(6'b100011), .b(MPC_q), .eq(WE_RAM));  // open: gt, lt
  Register #(.trigger("falling"), .width(17)) MIR (
    .D(rom_1_data), .en(1'b1), .clk(CLK),
    .Q({MUX_OPERAND2, WE_PC, WE_MBR, WE_OUT, WE_B, WE_A, OPCODE_ALU, MIR_q}), .clr(RESET));

  // Other names for the same wires on the sheet: R = RESET

  // Notes on the sheet:
  //   Mux for next microinstruction, either from RAM
  //    or decided by last microinstrution
  //   Address BEQ (Part 2)
  //   Address BSKIP
  //   JMPC
  //   NEXT
  //   Address JMP
  //   Mux for branch (conditional jump)
  //   Address STORE (Part HW)
  //   contents of rom_1 (hex, n*v repeats v):
  //   2001 40 14180 3 18482 18882 1002 1082 502 982 602 682 702 782 802 14190 2011 c080 293 0 14182 14196
  //   2017 8482 14199 201a 1099b c09c 201d 849e 4080 141a0 2021 109a2 c0a3 24 4080
endmodule

module computer (
  input  [7:0] INPUT_BUS,
  input  RESET,
  output [7:0] QUTPUT
);

  wire clock_1_out, controlunit_1_we_a, controlunit_1_we_b, controlunit_1_we_mbr, controlunit_1_we_out,
       controlunit_1_we_pc, controlunit_1_we_ram, datapath_1_cmp;
  wire [1:0] controlunit_1_mux_operand2;
  wire [2:0] controlunit_1_opcode_alu;
  wire [5:0] datapath_1_instruction_code;
  wire [7:0] datapath_1_ram_address, datapath_1_ram_data, ram_1_dout;

  Hex_Digit_Display hex_digit_display_1 (.value(INPUT_BUS[7:4]));  // open: dp
  Hex_Digit_Display hex_digit_display_2 (.value(INPUT_BUS[3:0]));  // open: dp
  Clock clock_1 (.out(clock_1_out));
  controlunit controlunit_1 (
    .RESET(RESET), .CLK(clock_1_out), .INSTRUCTION_CODE(datapath_1_instruction_code), .CMP(datapath_1_cmp),
    .WE_RAM(controlunit_1_we_ram), .OPCODE_ALU(controlunit_1_opcode_alu), .WE_A(controlunit_1_we_a),
    .WE_B(controlunit_1_we_b), .WE_OUT(controlunit_1_we_out), .WE_MBR(controlunit_1_we_mbr),
    .WE_PC(controlunit_1_we_pc), .MUX_OPERAND2(controlunit_1_mux_operand2));
  RAM #(.trigger("falling")) ram_1 (
    .addr(datapath_1_ram_address), .we(controlunit_1_we_ram), .oe(1'b1), .clk(clock_1_out),
    .din(datapath_1_ram_data), .dout(ram_1_dout));
  datapath datapath_1 (
    .WE_OUT(controlunit_1_we_out), .RESET(RESET), .CLK(clock_1_out), .WE_A(controlunit_1_we_a),
    .EXTERNAL_MEMORY_DATA_BUS(ram_1_dout), .EXTERNAL_INPUT_BUS(INPUT_BUS), .WE_B(controlunit_1_we_b),
    .WE_MBR(controlunit_1_we_mbr), .WE_PC(controlunit_1_we_pc), .MUX_OPERAND2(controlunit_1_mux_operand2),
    .OPCODE_ALU(controlunit_1_opcode_alu), .RAM_DATA(datapath_1_ram_data), .OUTPUT_BUS(QUTPUT),
    .RAM_ADDRESS(datapath_1_ram_address), .INSTRUCTION_CODE(datapath_1_instruction_code), .CMP(datapath_1_cmp));
  Hex_Digit_Display hex_digit_display_3 (.value(QUTPUT[7:4]));  // open: dp
  Hex_Digit_Display hex_digit_display_4 (.value(QUTPUT[3:0]));  // open: dp
endmodule
